// Logisim project ProcesadorSimpleBase.circ as structural Verilog
module BR (
  input  wr,
  input  clk,
  input  reset,
  input  [2:0] DA,
  input  [2:0] DB,
  input  [2:0] DC,
  input  [15:0] C,
  output [15:0] A,
  output [15:0] B
);

  wire decoder_1_out1, decoder_1_out2, decoder_1_out3, decoder_1_out4, decoder_1_out5, decoder_1_out6,
       decoder_1_out7;
  wire [15:0] register_1_q, register_2_q, register_3_q, register_4_q, register_5_q, register_6_q,
       register_7_q;

  Decoder #(.select(3), .disabled(0)) decoder_1 (
    .out1(decoder_1_out1), .out2(decoder_1_out2), .out3(decoder_1_out3), .out4(decoder_1_out4),
    .out5(decoder_1_out5), .out6(decoder_1_out6), .out7(decoder_1_out7), .sel(DC), .en(wr));  // open: out0
  Register #(.width(16)) register_1 (.D(C), .en(decoder_1_out1), .Q(register_1_q), .clk(clk), .clr(reset));
  Register #(.width(16)) register_2 (.D(C), .en(decoder_1_out2), .Q(register_2_q), .clk(clk), .clr(reset));
  Register #(.width(16)) register_3 (.D(C), .en(decoder_1_out3), .Q(register_3_q), .clk(clk), .clr(reset));
  Register #(.width(16)) register_4 (.D(C), .en(decoder_1_out4), .Q(register_4_q), .clk(clk), .clr(reset));
  Register #(.width(16)) register_5 (.D(C), .en(decoder_1_out5), .Q(register_5_q), .clk(clk), .clr(reset));
  Register #(.width(16)) register_6 (.D(C), .en(decoder_1_out6), .Q(register_6_q), .clk(clk), .clr(reset));
  Register #(.width(16)) register_7 (.D(C), .en(decoder_1_out7), .Q(register_7_q), .clk(clk), .clr(reset));
  Multiplexer #(.select(3), .width(16), .enable("false")) multiplexer_1 (
    .in0({16{1'b0}}), .in1(register_1_q), .in2(register_2_q), .in3(register_3_q), .in4(register_4_q),
    .in5(register_5_q), .in6(register_6_q), .in7(register_7_q), .out(A), .sel(DA));
  Multiplexer #(.select(3), .width(16), .enable("false")) multiplexer_2 (
    .in0({16{1'b0}}), .in1(register_1_q), .in2(register_2_q), .in3(register_3_q), .in4(register_4_q),
    .in5(register_5_q), .in6(register_6_q), .in7(register_7_q), .out(B), .sel(DB));
endmodule

module ALU (
  input  [1:0] Op,
  input  [15:0] A,
  input  [15:0] B,
  output [15:0] OUT
);

  wire [15:0] adder_1_out, and_1_out, or_1_out, subtractor_1_out;

  Adder #(.width(16)) adder_1 (.a(A), .b(B), .out(adder_1_out));  // open: cin, cout
  Subtractor #(.width(16)) subtractor_1 (.a(A), .b(B), .out(subtractor_1_out));  // open: bin, bout
  assign and_1_out = A & B;  // AND_Gate and_1, 16 bits wide
  assign or_1_out = A | B;  // OR_Gate or_1, 16 bits wide
  Multiplexer #(.select(2), .width(16), .enable("false")) multiplexer_1 (
    .in0(adder_1_out), .in1(subtractor_1_out), .in2(and_1_out), .in3(or_1_out), .out(OUT), .sel(Op));
endmodule

module MEMDAT (
  input  [15:0] ADDR,
  input  [15:0] DATAIN,
  input  wr,
  input  clk,
  input  reset,
  output [15:0] DATAOUT
);

  RAM #(.dataWidth(16), .bus("separate"), .Datafile_on_reset("datos.txt")) ram_1 (
    .addr(ADDR[7:0]), .din(DATAIN), .data(DATAOUT), .str(wr), .clk(clk), .clr(reset));  // open: sel, ld
endmodule

module MEMINST (
  input  [15:0] ADDR,
  output [15:0] INST
);

  RAM #(.dataWidth(16), .bus("separate"), .Datafile_on_reset("instrucciones.txt")) ram_1 (
    .addr(ADDR[7:0]), .data(INST));  // open: din, str, sel, clk, ld, clr
endmodule
